// Logisim project 6651071098_LAB1_Bai3.circ as structural Verilog: 2 circuits, main circuit main
module main (
  input  [3:0] A_3_0,
  input  [3:0] B_3_0,
  output Cout,
  output [3:0] Sum_3_0
);

  wire fa_1bit_1_cout, fa_1bit_2_cout, fa_1bit_3_cout;

  FA_1bit fa_1bit_1 (.A(A_3_0[0]), .B(B_3_0[0]), .Cin(1'b0), .S(Sum_3_0[0]), .Cout(fa_1bit_1_cout));
  FA_1bit fa_1bit_2 (.A(A_3_0[1]), .B(B_3_0[1]), .Cin(fa_1bit_1_cout), .S(Sum_3_0[1]), .Cout(fa_1bit_2_cout));
  FA_1bit fa_1bit_3 (.A(A_3_0[2]), .B(B_3_0[2]), .Cin(fa_1bit_2_cout), .S(Sum_3_0[2]), .Cout(fa_1bit_3_cout));
  FA_1bit fa_1bit_4 (.A(A_3_0[3]), .B(B_3_0[3]), .Cin(fa_1bit_3_cout), .S(Sum_3_0[3]), .Cout(Cout));

  // Notes on the sheet:
  //   LeVoDucHuy_6651071098
endmodule

module FA_1bit (
  input  A,
  input  B,
  input  Cin,
  output S,
  output Cout
);

  wire and_1_out, and_2_out, xor_1_p3;

  // XOR_Gate xor_1: pin names not known; wires that end beside it: B, A, xor_1_p3
  and and_1 (and_1_out, A, B);
  // XOR_Gate xor_2: pin names not known; wires that end beside it: xor_1_p3, Cin, S
  and and_2 (and_2_out, xor_1_p3, Cin);
  or or_1 (Cout, and_2_out, and_1_out);
endmodule
