// Logisim project 6651071098_LAB2_Bai1.circ as structural Verilog: 1 circuit, main circuit main
module main (
  input  A2,
  input  A1,
  input  A0,
  input  EN,
  output Y0,
  output Y1,
  output Y2,
  output Y3,
  output Y4,
  output Y5,
  output Y6,
  output Y7
);

  Decoder #(.select(3), .disabled(0)) decoder_1 (
    .out0(Y0), .out1(Y1), .out2(Y2), .out3(Y3), .out4(Y4), .out5(Y5), .out6(Y6), .out7(Y7),
    .sel({A2, A1, A0}), .en(EN));

  // Notes on the sheet:
  //   LeVoDucHuy_6651071098
endmodule
