// Logisim project 6651071098_LAB2_Bai2.circ as structural Verilog: 1 circuit, main circuit main
// 2
module main (
  input  A,
  input  B,
  input  C,
  output Y
);

  wire xor_1_out;

  xor xor_1 (xor_1_out, A, B);
  and and_1 (Y, xor_1_out, C);

  // Notes on the sheet:
  //   LeVoDucHuy_6651071098
endmodule
