// Logisim project 6651071098_LAB2_Bai5.circ as structural Verilog: 1 circuit, main circuit main
module main (
  input  [3:0] A_3_0,
  input  [3:0] B_3_0,
  output A_B,
  output A_B_2,
  output A_B_3
);

  Comparator #(.width(4), .mode("unsigned")) comparator_1 (.a(A_3_0), .b(B_3_0), .gt(A_B), .eq(A_B_2), .lt(A_B_3));

  // Notes on the sheet:
  //   LeVoDucHuy_6651071098
endmodule
