// Logisim project 6651071098_LAB2_Bai6.circ as structural Verilog: 1 circuit, main circuit main
module main (
  input  Enable,
  input  Reset,
  output [3:0] Q_3_0
);

  wire CLK_out, d_ff_4_q;

  Clock CLK (.out(CLK_out));
  D_Flip_Flop d_ff_1 (.clk(CLK_out), .D(Reset), .Q(Reset), .Qn(Reset), .en(Enable), .reset(Reset));  // open: preset
  D_Flip_Flop d_ff_2 (.clk(Reset), .D(Reset), .Q(Reset), .Qn(Reset), .en(Enable), .reset(Reset));  // open: preset
  D_Flip_Flop d_ff_3 (.clk(Reset), .D(Reset), .Q(Reset), .Qn(Reset), .en(Enable), .reset(Reset));  // open: preset
  D_Flip_Flop d_ff_4 (.clk(Reset), .D(Reset), .Q(d_ff_4_q), .Qn(Reset), .en(Enable), .reset(Reset));  // open: preset

  assign Q_3_0[3:1] = {3{Reset}};

  // Notes on the sheet:
  //   LeVoDucHuy_6651071098
endmodule
