// Logisim project 6651071098_LAB2_Bai7.circ as structural Verilog: 1 circuit, main circuit main
module main (
  input  [2:0] Addr_2_0,
  input  [3:0] Data_3_0,
  input  Load_Write_Enable,
  output [3:0] Data_out_3_0
);

  wire CLK_out;

  Clock CLK (.out(CLK_out));
  RAM #(.addrWidth(3), .dataWidth(4), .bus("separate")) ram_1 (
    .addr(Addr_2_0), .din(Data_3_0), .data(Data_out_3_0), .str(Load_Write_Enable), .clk(CLK_out), .ld(1'b1),
    .clr(1'b0));  // open: sel

  // Notes on the sheet:
  //   LeVoDucHuy_6651071098
endmodule
